# Fritzing sketch EthMqtt (saved by Fritzing 1.0.0rc)

parts:
  Part1 = emonTx V4.0.4
  W5500_Module1 = W5500 Ethernet module [package="DIP (Dual Inline) [THT]"]

nets:
  3.3V: Part1.3.3V, W5500_Module1.3.3V
  GND: Part1.GND, W5500_Module1.GND
  N1: Part1.RFM_SEL, W5500_Module1.SCS
  N2: Part1.RFM_SCK, W5500_Module1.SCLK
  N3: Part1.RFM_MISO, W5500_Module1.MISO
  N4: Part1.RFM_MOSI, W5500_Module1.MOSI

custom parts:
  emonTx V4.0.4: openenergymonitor emonTx V4
  W5500 Ethernet module: W5500 based SPI Ethernet module for Arduino, etc.
